# Fritzing sketch wiring (saved by Fritzing 0.9.3b)
breadboards: 1

parts:
  Raspberry_Pi1 = Raspberry Pi 2
  LCD1 = LCD screen
  R1 = Trimmer Potentiometer [maximum_resistance=10kΩ package=THT]
  S1 = Round Pushbutton
  S2 = Round Pushbutton
  S3 = Round Pushbutton
  S4 = Round Pushbutton
  S5 = Round Pushbutton

nets:
  N1: Raspberry_Pi1.3v3, S1.leg0, S2.leg0, S3.leg0, S4.leg0, S5.leg0
  N2: Raspberry_Pi1.GPIO27, LCD1.RS
  N3: Raspberry_Pi1.GPIO22, LCD1.E, LCD1.DB1
  GND: Raspberry_Pi1.GND, LCD1.VSS, LCD1.R/W, LCD1.DB0, LCD1.LED-, R1.leg2
  N4: Raspberry_Pi1.GPIO5, LCD1.DB3, LCD1.DB4
  N5: Raspberry_Pi1.GPIO6, LCD1.DB5
  N6: Raspberry_Pi1.GPIO13, LCD1.DB6
  N7: Raspberry_Pi1.GPIO26, LCD1.DB7
  N8: Raspberry_Pi1.GPIO12, S5.leg1
  N9: Raspberry_Pi1.GPIO25, S4.leg1
  N10: Raspberry_Pi1.GPIO24, S3.leg1
  N11: Raspberry_Pi1.GPIO23, S2.leg1
  N12: Raspberry_Pi1.GPIO18, S1.leg1
  5V: Raspberry_Pi1.5V, LCD1.VDD, LCD1.LED+, R1.leg1
  N13: LCD1.V0, R1.wiper
